// Logisim project Decod Gray to Bin.circ as structural Verilog: 1 circuit, main circuit main
// s3
module main (
  input  _7,
  input  _6,
  input  _5,
  input  _4,
  input  _3,
  input  _2,
  input  _1,
  input  _0,
  input  _7_2,
  input  _6_2,
  input  _5_2,
  input  _4_2,
  input  _3_2,
  input  _2_2,
  input  _1_2,
  input  _0_2,
  output s,
  output s_2,
  output s_3,
  output s_4,
  output s_5,
  output s_6,
  output s_7,
  output s_8,
  output s_9,
  output s_10,
  output s_11,
  output s_12,
  output s_13,
  output s_14,
  output s_15,
  output s_16
);

  xor xor_1 (s_2, _7, _6);
  xor xor_2 (s_3, s_2, _5);
  xor xor_3 (s_4, s_3, _4);
  xor xor_4 (s_5, s_4, _3);
  xor xor_5 (s_6, s_5, _2);
  xor xor_6 (s_7, s_6, _1);
  xor xor_7 (s_8, s_7, _0);
  xor xor_8 (s_9, s_8, _7_2);
  xor xor_9 (s_10, s_9, _6_2);
  xor xor_10 (s_11, s_10, _5_2);
  xor xor_11 (s_12, s_11, _4_2);
  xor xor_12 (s_13, s_12, _3_2);
  xor xor_13 (s_14, s_13, _2_2);
  xor xor_14 (s_15, s_14, _1_2);
  xor xor_15 (s_16, s_15, _0_2);

  assign s = _7;
endmodule
