// Logisim project Estudo de MUX.circ as structural Verilog: 1 circuit, main circuit main
module main (
  input  [7:0] A,
  input  [7:0] B,
  input  [7:0] C,
  input  [7:0] D,
  input  [7:0] A_2,
  input  [7:0] B_2,
  input  [7:0] C_2,
  input  [7:0] D_2,
  input  [1:0] in_9,
  input  [1:0] in_10,
  output out_11,
  output out_12,
  output out_13,
  output [7:0] out_14,
  output out_15,
  output out_16,
  output out_17,
  output out_18,
  output out_19
);

  Multiplexer #(.select(2), .enable("false")) multiplexer_1 (
    .in0(A[0]), .in1(B[0]), .in2(C[0]), .in3(D[0]), .out(out_11), .sel(in_10));
  Multiplexer #(.select(2), .enable("false")) multiplexer_2 (
    .in0(A[1]), .in1(B[1]), .in2(C[1]), .in3(D[1]), .out(out_12), .sel(in_10));
  Multiplexer #(.select(2), .enable("false")) multiplexer_3 (
    .in0(A[2]), .in1(B[2]), .in2(C[2]), .in3(D[2]), .out(out_13), .sel(in_10));
  Multiplexer #(.select(2), .enable("false")) multiplexer_4 (
    .in0(A[3]), .in1(B[3]), .in2(C[3]), .in3(D[3]), .out(out_15), .sel(in_10));
  Multiplexer #(.select(2), .enable("false")) multiplexer_5 (
    .in0(A[4]), .in1(B[4]), .in2(C[4]), .in3(D[4]), .out(out_16), .sel(in_10));
  Multiplexer #(.select(2), .enable("false")) multiplexer_6 (
    .in0(A[5]), .in1(B[5]), .in2(C[5]), .in3(D[5]), .out(out_17), .sel(in_10));
  Multiplexer #(.select(2), .enable("false")) multiplexer_7 (
    .in0(A[6]), .in1(B[6]), .in2(C[6]), .in3(D[6]), .out(out_18), .sel(in_10));
  Multiplexer #(.select(2), .enable("false")) multiplexer_8 (
    .in0(A[7]), .in1(B[7]), .in2(C[7]), .in3(D[7]), .out(out_19), .sel(in_10));
  Multiplexer #(.select(2), .width(8), .enable("false")) multiplexer_9 (
    .in0(A_2), .in1(B_2), .in2(C_2), .in3(D_2), .out(out_14), .sel(in_9));
endmodule
