// Logisim project Multiplexador 8x1 com buffer.circ as structural Verilog: 1 circuit, main circuit main
module main (
  input  in_1,
  input  in_2,
  input  in_3,
  input  in_4,
  input  in_5,
  input  in_6,
  input  in_7,
  input  in_8,
  input  in_9,
  input  in_10,
  input  in_11,
  output out_12
);

  wire and_1_out, and_2_out, and_3_out, and_4_out, and_5_out, and_6_out, and_7_out, and_8_out, and_9_out,
       and_10_out, and_11_out, and_12_out;

  assign out_12 = and_1_out ? in_1 : 1'bz;  // Controlled_Buffer controlled_buffer_1
  and and_1 (and_1_out, and_2_out, ~in_9);  // AND_Gate
  and and_2 (and_2_out, ~in_10, ~in_11);  // AND_Gate
  assign out_12 = and_3_out ? in_2 : 1'bz;  // Controlled_Buffer controlled_buffer_2
  and and_3 (and_3_out, and_5_out, ~in_9);  // AND_Gate
  and and_4 (and_4_out, in_10, ~in_11);  // AND_Gate
  and and_5 (and_5_out, ~in_10, in_11);  // AND_Gate
  assign out_12 = and_6_out ? in_3 : 1'bz;  // Controlled_Buffer controlled_buffer_3
  and and_6 (and_6_out, and_4_out, ~in_9);  // AND_Gate
  and and_7 (and_7_out, and_8_out, ~in_9);  // AND_Gate
  and and_8 (and_8_out, in_10, in_11);
  assign out_12 = and_7_out ? in_4 : 1'bz;  // Controlled_Buffer controlled_buffer_4
  assign out_12 = and_9_out ? in_5 : 1'bz;  // Controlled_Buffer controlled_buffer_5
  and and_9 (and_9_out, in_9, and_2_out);
  assign out_12 = and_10_out ? in_6 : 1'bz;  // Controlled_Buffer controlled_buffer_6
  and and_10 (and_10_out, in_9, and_5_out);
  assign out_12 = and_11_out ? in_7 : 1'bz;  // Controlled_Buffer controlled_buffer_7
  and and_11 (and_11_out, in_9, and_4_out);
  assign out_12 = and_12_out ? in_8 : 1'bz;  // Controlled_Buffer controlled_buffer_8
  and and_12 (and_12_out, in_9, and_8_out);
endmodule
