// Logisim project 987654321 ERROR 8 BITS.circ as structural Verilog: 1 circuit, main circuit main
module main (
  input  in_1,
  input  in_2,
  input  in_3,
  input  in_4,
  input  in_5,
  input  in_6,
  input  in_7,
  input  in_8,
  input  in_9,
  input  in_10,
  output E
);

  wire or_1_out, xnor_1_out;

  or or_1 (or_1_out, in_1, in_5, in_9, in_8, in_7, in_6, in_4, in_3, in_10, in_2);
  and and_1 (E, or_1_out, xnor_1_out);
  NotExactlyOne xnor_1 (
    .out(xnor_1_out), .in0(in_1), .in1(in_2), .in2(in_3), .in3(in_4), .in4(in_5), .in5(in_6), .in6(in_7),
    .in7(in_8), .in8(in_9), .in9(in_10));
endmodule
