// Logisim project BCD  ERROR 8 BITS.circ as structural Verilog: 1 circuit, main circuit main
module main (
  input  i7,
  input  i6,
  input  i5,
  input  i4,
  input  i3,
  input  i2,
  input  i1,
  input  i0,
  output S7,
  output S6,
  output S5,
  output S4,
  output E,
  output S3,
  output S2,
  output S1,
  output S0
);

  wire and_1_out, and_2_out, and_3_out, and_4_out, or_1_out, or_2_out;

  and and_1 (and_1_out, i7, i5);
  and and_2 (and_2_out, i7, i6);
  and and_3 (and_3_out, i3, i1);
  and and_4 (and_4_out, i3, i2);
  or or_1 (or_1_out, and_1_out, and_2_out);
  or or_2 (or_2_out, and_3_out, and_4_out);
  or or_3 (E, or_1_out, or_2_out);

  assign S0 = i0;
  assign S1 = i1;
  assign S2 = i2;
  assign S3 = i3;
  assign S4 = i4;
  assign S5 = i5;
  assign S6 = i6;
  assign S7 = i7;
endmodule
