// Logisim project Decod Bin to BCD.circ as structural Verilog: 3 circuits, main circuit Circuit Decoded
module Circuit_Decoded (
  input  [6:0] in_1,
  output [3:0] out_2,
  output [3:0] out_3
);

  wire bcd_error_1_e, decoded_1_s0, decoded_1_s1, decoded_1_s2, decoded_1_s3, decoded_1_s4, decoded_1_s5,
       decoded_1_s6, decoded_1_s7, not_1_out, not_2_out;
  wire [3:0] bcd_error_1_s0, bcd_error_1_s4;

  Decoded decoded_1 (
    .S7(decoded_1_s7), .S6(decoded_1_s6), .S5(decoded_1_s5), .S4(decoded_1_s4), .S3(decoded_1_s3),
    .S2(decoded_1_s2), .S1(decoded_1_s1), .S0(decoded_1_s0), .in_1(in_1[6]), .in_2(in_1[5]), .in_3(in_1[4]),
    .in_4(in_1[3]), .in_5(in_1[2]), .in_6(in_1[1]), .in_7(in_1[0]));
  BCD_ERROR bcd_error_1 (
    .S7(bcd_error_1_s4[3]), .S6(bcd_error_1_s4[2]), .S5(bcd_error_1_s4[1]), .S4(bcd_error_1_s4[0]),
    .E(bcd_error_1_e), .S3(bcd_error_1_s0[3]), .S2(bcd_error_1_s0[2]), .S1(bcd_error_1_s0[1]),
    .S0(bcd_error_1_s0[0]), .i7(decoded_1_s7), .i3(decoded_1_s3), .i6(decoded_1_s6), .i2(decoded_1_s2),
    .i5(decoded_1_s5), .i1(decoded_1_s1), .i4(decoded_1_s4), .i0(decoded_1_s0));
  assign out_2 = not_1_out ? bcd_error_1_s4 : 4'bz;  // Controlled_Buffer controlled_buffer_1
  not not_1 (not_1_out, bcd_error_1_e);
  assign out_3 = not_2_out ? bcd_error_1_s0 : 4'bz;  // Controlled_Buffer controlled_buffer_2
  not not_2 (not_2_out, bcd_error_1_e);
endmodule

module BCD_ERROR (
  input  i7,
  input  i6,
  input  i5,
  input  i4,
  input  i3,
  input  i2,
  input  i1,
  input  i0,
  output S7,
  output S6,
  output S5,
  output S4,
  output E,
  output S3,
  output S2,
  output S1,
  output S0
);

  wire and_1_out, and_2_out, and_3_out, and_4_out, or_1_out, or_2_out;

  and and_1 (and_1_out, i7, i5);
  and and_2 (and_2_out, i7, i6);
  and and_3 (and_3_out, i3, i1);
  and and_4 (and_4_out, i3, i2);
  or or_1 (or_1_out, and_1_out, and_2_out);
  or or_2 (or_2_out, and_3_out, and_4_out);
  or or_3 (E, or_1_out, 1'b0);

  assign S0 = i0;
  assign S1 = i1;
  assign S2 = i2;
  assign S3 = i3;
  assign S4 = i4;
  assign S5 = i5;
  assign S6 = i6;
  assign S7 = i7;
endmodule

module Decoded (
  input  in_1,
  input  in_2,
  input  in_3,
  input  in_4,
  input  in_5,
  input  in_6,
  input  in_7,
  output S7,
  output S6,
  output S5,
  output S4,
  output S3,
  output S2,
  output S1,
  output S0
);

  wire [6:0] undriven;
  wire [6:4] divider_1_out, divider_1_rem;

  // Probe on {in_1, in_2, in_3, in_4, in_5, in_6, in_7}
  Divider #(.width(7)) divider_1 (
    .a({in_1, in_2, in_3, in_4, in_5, in_6, in_7}), .b(7'b0001010), .out({divider_1_out, S7, S6, S5, S4}),
    .upper(undriven), .rem({divider_1_rem, S3, S2, S1, S0}));
endmodule
