// Logisim project Decod Bin to Gray.circ as structural Verilog: 1 circuit, main circuit main
module main (
  input  _7,
  input  _6,
  input  _5,
  input  _4,
  input  _3,
  input  _2,
  input  _1,
  input  _0,
  output s7,
  output s6,
  output s5,
  output s4,
  output s3,
  output s2,
  output s1,
  output s0
);

  xor xor_1 (s6, _7, _6);
  xor xor_2 (s5, _6, _5);
  xor xor_3 (s4, _5, _4);
  xor xor_4 (s3, _4, _3);
  xor xor_5 (s2, _3, _2);
  xor xor_6 (s1, _2, _1);
  xor xor_7 (s0, _1, _0);

  assign s7 = _7;
endmodule
