// Logisim project Ex de 3 ERROR 8 BITS.circ as structural Verilog: 1 circuit, main circuit main
module main (
  input  in_1,
  input  in_2,
  input  in_3,
  input  in_4,
  output E
);

  wire and_1_out, and_2_out, and_3_out, and_4_out;

  and and_1 (and_1_out, ~in_1, ~in_2, ~in_3);  // AND_Gate
  and and_2 (and_2_out, ~in_1, ~in_2, ~in_4);  // AND_Gate
  and and_3 (and_3_out, in_1, in_2, in_3);
  and and_4 (and_4_out, in_1, in_2, in_4);
  or or_1 (E, and_1_out, and_2_out, and_3_out, and_4_out);
endmodule
