// Logisim project Multiplicador + & - (1 somador).circ as structural Verilog: 1 circuit, main circuit main
module main (
  input  [7:0] A,
  input  RESET,
  input  [7:0] B
);

  wire Clock_out, comparator_1_lt, comparator_2_lt, not_1_out, not_2_out;
  wire [7:0] Contador_q, controlled_buffer_1_out, controlled_buffer_4_out;
  wire [15:0] adder_1_out, bit_extender_1_out, controlled_buffer_2_out, controlled_buffer_3_out,
       Registrador_q;

  assign bit_extender_1_out = {{8{A[7]}}, A};  // Bit_Extender bit_extender_1
  not not_1 (not_1_out, comparator_1_lt);
  Comparator comparator_1 (.a(B), .b({8{1'b0}}), .lt(comparator_1_lt));  // open: gt, eq
  not not_2 (not_2_out, comparator_1_lt);
  assign controlled_buffer_1_out = comparator_1_lt ? B : 8'bz;  // Controlled_Buffer controlled_buffer_1
  Adder #(.width(16)) adder_1 (.a(bit_extender_1_out), .b(Registrador_q), .out(adder_1_out));  // open: cin, cout
  assign controlled_buffer_2_out = not_1_out ? Registrador_q : 16'bz;  // Controlled_Buffer controlled_buffer_2
  assign controlled_buffer_3_out = comparator_1_lt ? Registrador_q : 16'bz;  // Controlled_Buffer controlled_buffer_3
  assign controlled_buffer_4_out = not_2_out ? B : 8'bz;  // Controlled_Buffer controlled_buffer_4
  Negator negator_1 (.in(controlled_buffer_1_out), .out(controlled_buffer_4_out));
  // Probe on controlled_buffer_2_out
  Negator #(.width(16)) negator_2 (.in(controlled_buffer_3_out), .out(controlled_buffer_2_out));
  Register #(.width(16)) Registrador (
    .D(adder_1_out), .en(comparator_2_lt), .Q(Registrador_q), .clk(Clock_out), .clr(RESET));
  Clock Clock (.out(Clock_out));
  Counter #(.ongoal("stay")) Contador (.Q(Contador_q), .clk(Clock_out), .clr(RESET));  // open: load, D, count, carry
  Comparator #(.mode("unsigned")) comparator_2 (
    .a(Contador_q), .b(controlled_buffer_4_out), .lt(comparator_2_lt));  // open: gt, eq
endmodule
