// Logisim project circuito codigo jhonson.circ as structural Verilog: 1 circuit, main circuit main
module main (
  output Q0,
  output out_2,
  output out_3,
  output out_4,
  output Q4
);

  wire clock_1_out, d_ff_5_qn;

  Clock clock_1 (.out(clock_1_out));
  D_Flip_Flop d_ff_1 (.clk(clock_1_out), .D(d_ff_5_qn), .Q(Q0));  // open: Qn, preset, en, reset
  D_Flip_Flop d_ff_2 (.clk(clock_1_out), .D(Q0), .Q(out_2));  // open: Qn, preset, en, reset
  D_Flip_Flop d_ff_3 (.clk(clock_1_out), .D(out_2), .Q(out_3));  // open: Qn, preset, en, reset
  D_Flip_Flop d_ff_4 (.clk(clock_1_out), .D(out_3), .Q(out_4));  // open: Qn, preset, en, reset
  D_Flip_Flop d_ff_5 (.clk(clock_1_out), .D(out_4), .Q(Q4), .Qn(d_ff_5_qn));  // open: preset, en, reset
endmodule
