// Logisim project contador crescente  (borda de descida).circ as structural Verilog: 1 circuit, main circuit main
module main (
  output Q0,
  output out_2,
  output out_3,
  output Q3
);

  wire clock_1_out;

  Clock clock_1 (.out(clock_1_out));
  T_Flip_Flop #(.trigger("falling")) t_ff_1 (.clk(clock_1_out), .T(1'b1), .Q(Q0));  // open: Qn, preset, reset, en
  T_Flip_Flop #(.trigger("falling")) t_ff_2 (.clk(Q0), .T(1'b1), .Q(out_2));  // open: Qn, preset, reset, en
  T_Flip_Flop #(.trigger("falling")) t_ff_3 (.clk(out_2), .T(1'b1), .Q(out_3));  // open: Qn, preset, reset, en
  T_Flip_Flop #(.trigger("falling")) t_ff_4 (.clk(out_3), .T(1'b1), .Q(Q3));  // open: Qn, preset, reset, en
endmodule
